# Fritzing sketch ArduinoLeonardoSketch (saved by Fritzing 0.9.3b)

parts:
  Часть2 = Arduino Leonardo (Rev3b)
  Throttle_pot1 = Rotary Encoder [package=THT]
  Breake_pot_(if_LC*_-_then_clutch_pot)1 = Rotary Encoder [package=THT]
  Clutch_pot_(if_LC*_-_then_handbreake_pot)1 = Rotary Encoder [package=THT]
  Handbreake_pot_(if_LC*_-_then_botton0)1 = Rotary Encoder [package=THT]
  ENCODER1 = YumoE6B2
  Button_3 = Round Pushbutton
  Button_4 = Round Pushbutton

nets:
  N1: Часть2.D0/RX, ENCODER1.B
  N2: Часть2.D1/TX, ENCODER1.A
  N3: Часть2.D2/SDA, ENCODER1.Z
  N4: Часть2.5V, Throttle_pot1.EncoderPinB
  N5: Часть2.GND, Throttle_pot1.EncoderPinA
  N6: Часть2.A0, Throttle_pot1.EncoderPinC
  N7: Часть2.A1, Breake_pot_(if_LC*_-_then_clutch_pot)1.EncoderPinC
  N8: Часть2.A2, Clutch_pot_(if_LC*_-_then_handbreake_pot)1.EncoderPinC
  N9: Часть2.A3, Handbreake_pot_(if_LC*_-_then_botton0)1.EncoderPinC
  N10: Часть2.A4, Button_4.leg0
  N11: Часть2.A5, Button_3.leg0

notes:
  Button 1,2 (fw-v180 only)
  LC - load cell with HX711 (fw-w182)

custom parts:
  YumoE6B2: Yumo E6B2-C incremental encoder. Resolutions 10 to 4000 pulses per revolution (depending on model number). Power from 5 to 24V (again depending on model). Dia 40mm body 30mm plus 20mm shaft.
